# Fritzing sketch NotAutorouted (saved by Fritzing 0.9.4)

parts:
  MCU1 = Raspberry Pi Zero
  OLED1 = OLED 128x64 I2C Monochrome Display
  OLED2 = OLED 128x64 I2C Monochrome Display
  S1 = Pushbutton [package="[THT]"]
  S2 = Pushbutton [package="[THT]"]

nets:
  VDD: MCU1.pin_2, MCU1.pin_4, OLED1.VDD, OLED2.VDD
  N1: MCU1.pin_3, OLED1.SDA
  N2: MCU1.pin_5, OLED1.SCK
  GND: MCU1.pin_6, MCU1.pin_9, MCU1.pin_20, OLED1.GND, OLED2.GND, S1.Pin_1, S1.Pin_2, S2.Pin_1, S2.Pin_2
  N3: MCU1.pin_11, S1.Pin_3, S1.Pin_4
  N4: MCU1.pin_13, S2.Pin_3, S2.Pin_4
  N5: MCU1.pin_16, OLED2.SDA
  N6: MCU1.pin_18, OLED2.SCK
